// Logisim project CALCULADORA DE SOMA-4bits.circ as structural Verilog
module _1_2___SOMADOR (
  input  a0,
  input  b0,
  output s0,
  output cout
);

  xor xor_1 (s0, b0, a0);
  and and_1 (cout, a0, b0);
endmodule

module SOMADOR (
  input  a0,
  input  b0,
  input  cin,
  output s0,
  output cout
);

  wire n1_2_somador_1_cout, n1_2_somador_1_s0, n1_2_somador_2_cout;

  _1_2___SOMADOR u_1_2_somador_1 (.a0(a0), .b0(b0), .s0(n1_2_somador_1_s0), .cout(n1_2_somador_1_cout));
  _1_2___SOMADOR u_1_2_somador_2 (.a0(n1_2_somador_1_s0), .b0(cin), .s0(s0), .cout(n1_2_somador_2_cout));
  or or_1 (cout, n1_2_somador_2_cout, n1_2_somador_1_cout);
endmodule

module SOMADOR___4_BITS (
  input  cin,
  input  a0,
  input  b0,
  input  a1,
  input  b1,
  input  a2,
  input  b2,
  input  a3,
  input  b3,
  output s0,
  output s1,
  output s2,
  output s3,
  output cout
);

  wire somador_1_cout, somador_2_cout, somador_3_cout;

  SOMADOR somador_1 (.a0(a0), .b0(b0), .cin(cin), .s0(s0), .cout(somador_1_cout));
  SOMADOR somador_2 (.a0(a1), .b0(b1), .cin(somador_1_cout), .s0(s1), .cout(somador_2_cout));
  SOMADOR somador_3 (.a0(a2), .b0(b2), .cin(somador_2_cout), .s0(s2), .cout(somador_3_cout));
  SOMADOR somador_4 (.a0(a3), .b0(b3), .cin(somador_3_cout), .s0(s3), .cout(cout));
endmodule

module CALCULADORA___4_BITS (
  input  A3,
  input  A2,
  input  A1,
  input  A0,
  input  Cin,
  input  B3,
  input  B2,
  input  B1,
  input  B0,
  output S3,
  output S2,
  output S1,
  output S0,
  output Cout
);

  wire decodificador_1_a, decodificador_1_b, decodificador_1_c, decodificador_1_d, decodificador_1_e,
       decodificador_1_f, decodificador_1_g, decodificador_2_a, decodificador_2_b, decodificador_2_c,
       decodificador_2_d, decodificador_2_e, decodificador_2_f, decodificador_2_g, decodificador_3_a,
       decodificador_3_b, decodificador_3_c, decodificador_3_d, decodificador_3_e, decodificador_3_f,
       decodificador_3_g;

  DECODIFICADOR decodificador_1 (
    .E3(A3), .E2(A2), .E1(A1), .E0(A0), .a(decodificador_1_a), .b(decodificador_1_b), .c(decodificador_1_c),
    .d(decodificador_1_d), .e(decodificador_1_e), .f(decodificador_1_f), .g(decodificador_1_g));
  DECODIFICADOR decodificador_2 (
    .E3(B3), .E2(B2), .E1(B1), .E0(B0), .a(decodificador_2_a), .b(decodificador_2_b), .c(decodificador_2_c),
    .d(decodificador_2_d), .e(decodificador_2_e), .f(decodificador_2_f), .g(decodificador_2_g));
  _7_Segment_Display u_7_segment_display_1 (
    .g(decodificador_1_g), .f(decodificador_1_f), .a(decodificador_1_a), .b(decodificador_1_b),
    .e(decodificador_1_e), .d(decodificador_1_d), .c(decodificador_1_c));  // open: dp
  _7_Segment_Display u_7_segment_display_2 (
    .g(decodificador_2_g), .f(decodificador_2_f), .a(decodificador_2_a), .b(decodificador_2_b),
    .e(decodificador_2_e), .d(decodificador_2_d), .c(decodificador_2_c));  // open: dp
  SOMADOR___4_BITS somador_4_bits_1 (
    .a0(A0), .b0(B0), .a1(A1), .b1(B1), .a2(A2), .b2(B2), .a3(A3), .b3(B3), .s0(S0), .s1(S1), .s2(S2),
    .s3(S3), .cout(Cout), .cin(Cin));
  DECODIFICADOR decodificador_3 (
    .E3(S3), .E2(S2), .E1(S1), .E0(S0), .a(decodificador_3_a), .b(decodificador_3_b), .c(decodificador_3_c),
    .d(decodificador_3_d), .e(decodificador_3_e), .f(decodificador_3_f), .g(decodificador_3_g));
  _7_Segment_Display u_7_segment_display_3 (
    .g(decodificador_3_g), .f(decodificador_3_f), .a(decodificador_3_a), .b(decodificador_3_b),
    .e(decodificador_3_e), .d(decodificador_3_d), .c(decodificador_3_c));  // open: dp
endmodule

module DECODIFICADOR (
  input  E3,
  input  E2,
  input  E1,
  input  E0,
  output a,
  output b,
  output c,
  output d,
  output e,
  output f,
  output g
);

  wire and_1_out, and_2_out, and_3_out, and_4_out, and_5_out, and_6_out, and_7_out, and_8_out, and_9_out,
       and_10_out, and_11_out, and_12_out, and_13_out, and_14_out, and_15_out, and_16_out, and_17_out,
       and_18_out, and_19_out, and_20_out, and_21_out, and_22_out, and_23_out, and_24_out, and_25_out,
       and_26_out, and_27_out, and_28_out, and_29_out, and_30_out, and_31_out, and_32_out, and_33_out,
       and_34_out, and_35_out, and_36_out, not_1_out, not_2_out, not_3_out, not_4_out, not_5_out, not_6_out,
       not_7_out, not_8_out, not_9_out, not_10_out, not_11_out, not_12_out, not_13_out, not_14_out,
       not_15_out, not_16_out, not_17_out, not_18_out, not_19_out, not_20_out, not_21_out, not_22_out,
       not_23_out, not_24_out, not_25_out, not_26_out, not_27_out, not_28_out, not_29_out, not_30_out,
       not_31_out, not_32_out, not_33_out, not_34_out, not_35_out, not_36_out, not_37_out, not_38_out,
       not_39_out, not_40_out, not_41_out, not_42_out, not_43_out, not_44_out, not_45_out;

  not not_1 (not_1_out, E2);
  and and_1 (and_1_out, not_1_out, not_2_out);
  not not_2 (not_2_out, E0);
  not not_3 (not_3_out, E3);
  and and_2 (and_2_out, not_3_out, E1);
  not not_4 (not_4_out, E3);
  and and_3 (and_3_out, not_4_out, E2, E0);
  and and_4 (and_4_out, E2, E1);
  not not_5 (not_5_out, E2);
  and and_5 (and_5_out, E3, not_5_out, not_6_out);
  not not_6 (not_6_out, E1);
  and and_6 (and_6_out, E3, not_7_out);
  not not_7 (not_7_out, E0);
  not not_8 (not_8_out, E3);
  and and_7 (and_7_out, not_8_out, not_9_out);
  not not_9 (not_9_out, E2);
  not not_10 (not_10_out, E3);
  and and_8 (and_8_out, not_10_out, not_11_out, not_12_out);
  not not_11 (not_11_out, E1);
  not not_12 (not_12_out, E0);
  not not_13 (not_13_out, E2);
  and and_9 (and_9_out, not_13_out, not_14_out);
  not not_14 (not_14_out, E1);
  not not_15 (not_15_out, E2);
  and and_10 (and_10_out, not_15_out, not_16_out);
  not not_16 (not_16_out, E0);
  not not_17 (not_17_out, E3);
  and and_11 (and_11_out, not_17_out, E1, E0);
  not not_18 (not_18_out, E1);
  and and_12 (and_12_out, E3, not_18_out, E0);
  not not_19 (not_19_out, E3);
  and and_13 (and_13_out, not_19_out, not_20_out);
  not not_20 (not_20_out, E1);
  not not_21 (not_21_out, E3);
  and and_14 (and_14_out, not_21_out, E0);
  not not_22 (not_22_out, E1);
  and and_15 (and_15_out, not_22_out, E0);
  not not_23 (not_23_out, E3);
  and and_16 (and_16_out, not_23_out, E2);
  and and_17 (and_17_out, E3, not_24_out);
  not not_24 (not_24_out, E2);
  not not_25 (not_25_out, E3);
  and and_18 (and_18_out, not_25_out, not_26_out, not_27_out);
  not not_26 (not_26_out, E2);
  not not_27 (not_27_out, E0);
  not not_28 (not_28_out, E2);
  and and_19 (and_19_out, not_28_out, E1, E0);
  and and_20 (and_20_out, E2, not_29_out, E0);
  not not_29 (not_29_out, E1);
  and and_21 (and_21_out, E2, E1, not_30_out);
  not not_30 (not_30_out, E0);
  and and_22 (and_22_out, E3, not_31_out);
  not not_31 (not_31_out, E1);
  not not_32 (not_32_out, E2);
  and and_23 (and_23_out, not_32_out, not_33_out);
  not not_33 (not_33_out, E0);
  and and_24 (and_24_out, E1, not_34_out);
  not not_34 (not_34_out, E0);
  and and_25 (and_25_out, E3, E1);
  and and_26 (and_26_out, E3, E2);
  not not_35 (not_35_out, E1);
  and and_27 (and_27_out, not_35_out, not_36_out);
  not not_36 (not_36_out, E0);
  not not_37 (not_37_out, E3);
  and and_28 (and_28_out, not_37_out, E2, not_38_out);
  not not_38 (not_38_out, E1);
  and and_29 (and_29_out, E2, not_39_out);
  not not_39 (not_39_out, E0);
  and and_30 (and_30_out, E3, not_40_out);
  not not_40 (not_40_out, E2);
  and and_31 (and_31_out, E3, E1);
  not not_41 (not_41_out, E2);
  and and_32 (and_32_out, not_41_out, E1);
  and and_33 (and_33_out, E1, not_42_out);
  not not_42 (not_42_out, E0);
  not not_43 (not_43_out, E3);
  and and_34 (and_34_out, not_43_out, E2, not_44_out);
  not not_44 (not_44_out, E1);
  and and_35 (and_35_out, E3, not_45_out);
  not not_45 (not_45_out, E2);
  and and_36 (and_36_out, E3, E0);
  or or_1 (c, and_13_out, and_14_out, and_15_out, and_16_out, and_17_out);
  or or_2 (d, and_18_out, and_19_out, and_20_out, and_21_out, and_22_out);
  or or_3 (e, and_23_out, and_24_out, and_25_out, and_26_out);
  or or_4 (f, and_27_out, and_28_out, and_29_out, and_30_out, and_31_out);
  or or_5 (g, and_32_out, and_33_out, and_34_out, and_35_out, and_36_out);
  or or_6 (a, and_1_out, and_2_out, and_3_out, and_4_out, and_5_out, and_6_out);
  or or_7 (b, and_7_out, and_8_out, and_9_out, and_10_out, and_11_out, and_12_out);
endmodule
