// Logisim project ULA.circ as structural Verilog
module _1_2___SOMADOR (
  input  A,
  input  B,
  output S0,
  output Cout
);

  xor xor_1 (S0, A, B);
  and and_1 (Cout, A, B);
endmodule

module SOMADOR (
  input  A,
  input  B,
  input  Cin,
  output S0,
  output Cout
);

  wire n1_2_somador_1_cout, n1_2_somador_1_s0, n1_2_somador_2_cout;

  _1_2___SOMADOR u_1_2_somador_1 (.A(A), .B(B), .S0(n1_2_somador_1_s0), .Cout(n1_2_somador_1_cout));
  _1_2___SOMADOR u_1_2_somador_2 (.A(n1_2_somador_1_s0), .B(Cin), .S0(S0), .Cout(n1_2_somador_2_cout));
  or or_1 (Cout, n1_2_somador_2_cout, n1_2_somador_1_cout);
endmodule

module ULA___1_BIT (
  input  A,
  input  B,
  input  Cin,
  input  [1:0] Opcode,
  input  Binvert,
  output S,
  output Cout
);

  wire and_1_out, multiplexer_1_out, not_1_out, not_2_out, or_1_out, somador_1_s0;

  Multiplexer #(.enable("false")) multiplexer_1 (.in0(B), .in1(not_1_out), .out(multiplexer_1_out), .sel(Binvert));
  not not_1 (not_1_out, B);
  and and_1 (and_1_out, A, multiplexer_1_out);
  or or_1 (or_1_out, A, multiplexer_1_out);
  not not_2 (not_2_out, A);
  SOMADOR somador_1 (.A(A), .B(multiplexer_1_out), .Cin(Cin), .S0(somador_1_s0), .Cout(Cout));
  Multiplexer #(.select(2), .enable("false")) multiplexer_2 (
    .in0(and_1_out), .in1(or_1_out), .in2(not_2_out), .in3(somador_1_s0), .out(S), .sel(Opcode));
endmodule

module ULA___74LS181 (
  input  [3:0] A,
  input  [3:0] B,
  input  [3:0] Opcode,
  output [3:0] out_4
);

  wire [3:0] and_1_out, and_2_out, and_3_out, nand_1_out, nor_1_out, not_1_out, not_2_out, or_1_out,
       or_2_out, or_3_out, xnor_1_out, xor_1_out;

  assign not_1_out = ~A;  // NOT_Gate not_1, 4 bits wide
  assign nor_1_out = ~(A | B);  // NOR_Gate nor_1, 4 bits wide
  assign and_1_out = ~A & B;  // AND_Gate and_1, 4 bits wide
  assign nand_1_out = ~(A & B);  // NAND_Gate nand_1, 4 bits wide
  assign not_2_out = ~B;  // NOT_Gate not_2, 4 bits wide
  assign xor_1_out = A ^ B;  // XOR_Gate xor_1, 4 bits wide
  assign and_2_out = A & ~B;  // AND_Gate and_2, 4 bits wide
  assign or_1_out = ~A | B;  // OR_Gate or_1, 4 bits wide
  assign xnor_1_out = ~(A ^ B);  // XNOR_Gate xnor_1, 4 bits wide
  assign and_3_out = A & B;  // AND_Gate and_3, 4 bits wide
  assign or_2_out = A | ~B;  // OR_Gate or_2, 4 bits wide
  assign or_3_out = A | B;  // OR_Gate or_3, 4 bits wide
  Multiplexer #(.select(4), .width(4), .enable("false")) multiplexer_1 (
    .in0(not_1_out), .in1(nor_1_out), .in2(and_1_out), .in3(4'b0000), .in4(nand_1_out), .in5(not_2_out),
    .in6(xor_1_out), .in7(and_2_out), .in8(or_1_out), .in9(xnor_1_out), .in10(B), .in11(and_3_out),
    .in12(4'b0001), .in13(or_2_out), .in14(or_3_out), .in15(A), .out(out_4), .sel(Opcode));
endmodule

module ULA___4_BITS (
  input  B3,
  input  B2,
  input  B1,
  input  B0,
  input  A3,
  input  A2,
  input  A1,
  input  A0,
  input  Binvert,
  input  [1:0] Opcode,
  output S0,
  output S1,
  output S2,
  output S3,
  output Cout
);

  wire ula_1_bit_1_cout, ula_1_bit_2_cout, ula_1_bit_3_cout;

  ULA___1_BIT ula_1_bit_1 (
    .Opcode(Opcode), .S(S0), .A(A0), .B(B0), .Cin(Binvert), .Binvert(Binvert), .Cout(ula_1_bit_1_cout));
  ULA___1_BIT ula_1_bit_2 (
    .Opcode(Opcode), .S(S1), .A(A1), .B(B1), .Cin(ula_1_bit_1_cout), .Binvert(Binvert),
    .Cout(ula_1_bit_2_cout));
  ULA___1_BIT ula_1_bit_3 (
    .Opcode(Opcode), .S(S2), .A(A2), .B(B2), .Cin(ula_1_bit_2_cout), .Binvert(Binvert),
    .Cout(ula_1_bit_3_cout));
  ULA___1_BIT ula_1_bit_4 (
    .Opcode(Opcode), .S(S3), .A(A3), .B(B3), .Cin(ula_1_bit_3_cout), .Binvert(Binvert), .Cout(Cout));

  // Notes on the sheet:
  //   Cin
endmodule
